# Fritzing sketch GaggiaPID (saved by Fritzing 0.9.4)
breadboards: 1

parts:
  Part1 = Adafruit Metro Mini [part_number="Adafruit #2590"]
  Part2 = OLED Monochrome 128x32 I2C [part_number=931]
  U1 = RELAY-SOLIDSTATE [package=relay-s108t02]
  Part3 = MCP9600
  S4 = Pushbutton [package="[SMD]"]
  S5 = Pushbutton [package="[SMD]"]
  S6 = Pushbutton [package="[SMD]"]

nets:
  N1: Part1.AD5/SCL, Part3.SCL
  N2: Part1.AD4/SDA, Part3.SDA
  N3: Part1.IO12, S4.Pin_1, S4.Pin_2, S5.Pin_3, S5.Pin_4, S6.Pin_3, S6.Pin_4
  N4: Part1.IO9, U1.+
  N5: Part1.IO5, S5.Pin_1, S5.Pin_2
  N6: Part1.IO3, S6.Pin_1, S6.Pin_2
  VIN: Part1.+5V, Part2.VIN, Part3.VIN
  GND: Part1.GND, Part2.GND, U1.-, Part3.GND, S4.Pin_3, S4.Pin_4

custom parts:
  Adafruit Metro Mini: We sure love the ATmega328 here at Adafruit, and we use them a lot for our own projects. The processor has plenty of GPIO, Analog inputs, hardware UART SPI and I2C, timers and PWM galore - just enough for most simple projects. When we need to go small, we use a Pro Trinket 3V or 5V, but if you want to have USB-to-Serial built in, we reach for an Adafruit METRO Mini. METRO Mini is the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
  OLED Monochrome 128x32 I2C: These displays are small, only about 1" diagonal, but very readable due to the high contrast of an OLED display. This display is made of 128x32 individual white OLED pixels, each one is turned on or off by the controller chip. Because the display makes its own light, no backlight is required. This reduces the power required to run the OLED and is why the display has such high contrast; we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
  MCP9600: Thermocouples are very sensitive, requiring a good amplifier with a cold-compensation reference. The Adafruit MCP9600 does all that for you, and can be easily interfaced with any microcontroller or single-board-computer with I2C. Inside, the chip handles all the analog stuff for you, and can interface with just about any thermocouple type: K, J, T, N, S, E, B and R type are all supported! You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
